# Fritzing sketch Crawler_01 (saved by Fritzing 0.7.5b)
breadboards: 1

parts:
  Arduino2 = Arduino
  IC1 = H-Bridge [package=THT]
  R2 = Resistor [tolerance=±5% resistance=220 package=THT]
  R3 = Resistor [tolerance=±5% resistance=220 package=THT]
  M1 = DC Motor
  M2 = DC Motor
  U1 = Voltage Regulator - 5V [package="TO220 [THT]"]

nets:
  GND: Arduino2.GND, IC1.GND1, IC1.GND2, IC1.GND3, IC1.GND4, U1.GND
  N1: Arduino2.D13, IC1.4A
  N2: Arduino2.D12, IC1.3A
  N3: Arduino2.D11, IC1.2A
  N4: Arduino2.D10, IC1.1A
  N5: Arduino2.+5V, R2.Pin_0, R3.Pin_1, U1.output_voltage
  N6: IC1.1_2EN, R3.Pin_0
  N7: IC1.1Y, M1.pin_2
  N8: IC1.2Y, M1.pin_1
  N9: IC1.3_4EN, R2.Pin_1
  N10: IC1.3Y, M2.pin_2
  N11: IC1.4Y, M2.pin_1
